# Fritzing sketch wiring (saved by Fritzing 0.9.3b)

parts:
  Adafruit_HUZZAH_ESP8266_Breakout1 = Adafruit HUZZAH ESP8266 Breakout [part_number=2471]
  LED1 = prefix0000

nets:
  N1: Adafruit_HUZZAH_ESP8266_Breakout1.GND, LED1.connector3
  N2: Adafruit_HUZZAH_ESP8266_Breakout1.V+, LED1.connector1
  N3: Adafruit_HUZZAH_ESP8266_Breakout1.#12, LED1.connector2
